# Fritzing sketch HIP_Schematic (saved by Fritzing 0.9.4)
breadboards: 1

parts:
  BLE_Module = Bluetooth HC-05 Macho
  Part4 = OBD II UART
  Part5 = Arduino Uno (Rev3)
  U1 = Voltage Regulator - Variable [package="TO220 [THT]"]
  Raspberry_Pi_1 = Raspberry Pi 3 [part_number=RPI-3-V1.2]
  X1 = USB Connectors [package=usb-minib]
  Camera = USB Connectors [package=usb-b-pth]
  Pressure_Pad = Textile Analog Pressure Sensor [part_number=PW073]
  R1 = Resistor [tolerance=±5% resistance=10k package="2512 [SMD]"]
  T1 = TMP36 Temperature Sensor [package="TO92 [THT]"]
  C1 = Ceramic Capacitor [capacitance=0.1mF package="0603 [SMD, multilayer]"]
  C2 = Ceramic Capacitor [capacitance=0.22mF package="0603 [SMD, multilayer]"]

nets:
  N1: BLE_Module.TXD, Raspberry_Pi_1.GIPO14
  N2: BLE_Module.RXD, Raspberry_Pi_1.GIPO15
  VCC: BLE_Module.VCC, Part5.VIN, U1.OUT, Raspberry_Pi_1.5V, Pressure_Pad.pin_1, T1.+Vs, C1.1
  GND: BLE_Module.GND, Part4.GND, Part5.GND, U1.ADJ, Raspberry_Pi_1.GND, R1.Pin_1, T1.GND, C1.0, C2.0
  CAN_H on Car: Part4.CAN_HI
  CAN_L on Car: Part4.CAN_LO
  N3: Part4.VBAT, U1.IN, C2.1
  N4: Part4.TX-O, Part5.D0/RX
  N5: Part4.RX-I, Part5.D1/TX
  N6: Part5.A0, Pressure_Pad.pin_0, R1.Pin_0
  N7: Part5.A1, T1.Vout
  N8: Part5.D8, Raspberry_Pi_1.GIPO27
  N9: X1.D+, Camera.D+
  N10: X1.D-, Camera.D-
  GND_2: X1.GND, Camera.GND
  N11: X1.VBUS, Camera.VBUS

notes:
  HIP Schematic
